# Fritzing sketch Motor_CW_CCW (saved by Fritzing 0.9.3b)

parts:
  IC1 = L293D [package=THT]
  Arduino1 = Arduino Uno (Rev3)
  M2 = DC Motor  # not connected
  BAT1 = 18650 battery holder [package=battery-18650-kit]
  BAT2 = 18650 battery holder [package=battery-18650-kit]
  BAT3 = 18650 battery holder [package=battery-18650-kit]

nets:
  N1: IC1.In_1, Arduino1.D6_PWM
  GND: IC1.0V, Arduino1.GND, BAT2.-
  N2: IC1.In_2, Arduino1.D5_PWM
  N3: IC1.+Vmotor, BAT1.+
  5V: IC1.+V, Arduino1.5V
  N4: BAT1.-, BAT3.+
  N5: BAT2.+, BAT3.-

custom parts:
  18650 battery holder: 18650 Battery Holder
