# Fritzing sketch My_Home (saved by Fritzing 0.9.3b)

parts:
  LED2 = LEDs [package=led10mm]
  Part2 = Lilypad Battery Connect
  Part3 = Arduino Uno (Rev3)
  KY-1 = Keyes Relay [package=THT]
  Part4 = HC-05 [part_number=HC-05 package="breakout board"]

nets:
  N1: LED2.A, Part2.-
  N2: LED2.C, KY-1.NO
  N3: Part2.+, KY-1.C
  N4: Part3.D8, KY-1.signal
  N5: Part3.D0/RX, Part4.TXD
  5V: Part3.5V, KY-1.power, Part4.VCC
  GND: Part3.GND, KY-1.ground, Part4.GND

notes:
  To
  Relay
  GND
  VCC
  230V AC Power Supply
  Phase
  Neutral
  To MC

custom parts:
  LEDs: LEDs Standard schematic elements and footprints for 5mm, 3mm, 1206, and 0603 sized LEDs. 5mm - Spark Fun Electronics SKU : COM-00529 (and others)
  Keyes Relay: The Keyes 5V relay module is suitable for SCM development, home appliance control. It uses a 5V~12V TIL control signal which can control DC / AC signal.
  HC-05: A commonly available HC-05 Bluetooth breakout board.
