# Fritzing sketch PIR_Alarm (saved by Fritzing 0.9.3b)

parts:
  PIR1 = PIR_sensor
  J1 = Piezo Speaker [part_number=batter]
  BATT1 = LiPoly Battery (1300mAh)

nets:
  N1: PIR1.connector1, BATT1.positive
  N2: PIR1.connector2, J1.pin2
  N3: PIR1.connector3, J1.pin1, BATT1.negative

custom parts:
  LiPoly Battery (1300mAh): Lithium Ion Polymer Battery (1300mAh)
