# Fritzing sketch Automatic_Unidirectional_Motor_Speed_Control (saved by Fritzing 0.9.3b)

parts:
  IC1 = L293D [package=THT]
  Arduino1 = Arduino Uno (Rev3)
  M2 = DC Motor  # not connected
  BAT1 = 18650 battery holder [package=battery-18650-kit]
  BAT2 = 18650 battery holder [package=battery-18650-kit]
  BAT3 = 18650 battery holder [package=battery-18650-kit]

nets:
  GND: IC1.In_1, IC1.0V, IC1.Out_3_(_Controlled_by_Enable_2_), Arduino1.GND, BAT2.-
  N1: IC1.In_2, Arduino1.D11_PWM/MOSI
  N2: IC1.+Vmotor, BAT1.+
  5V: IC1.In_4, IC1.+V, Arduino1.5V
  N3: BAT1.-, BAT3.+
  N4: BAT2.+, BAT3.-

custom parts:
  18650 battery holder: 18650 Battery Holder
