# Fritzing sketch IR_Switching (saved by Fritzing 0.9.3b)

parts:
  LED2 = LEDs [package=led10mm]
  Part2 = Lilypad Battery Connect
  Part3 = Arduino Uno (Rev3)
  KY-1 = Keyes Relay [package=THT]
  IR1 = TSOP312.., 314.. [part_number="TSOP 1738" package=THT]

nets:
  N1: LED2.A, Part2.-
  N2: LED2.C, KY-1.NO
  N3: Part2.+, KY-1.C
  N4: Part3.A0, IR1.GND
  N5: Part3.D8, KY-1.signal
  N6: Part3.3V3, KY-1.power
  N7: Part3.GND, KY-1.ground, IR1.Vs

notes:
  To
  Relay
  GND
  VCC
  230V AC Power Supply
  Phase
  Neutral
  To MC

custom parts:
  LEDs: LEDs Standard schematic elements and footprints for 5mm, 3mm, 1206, and 0603 sized LEDs. 5mm - Spark Fun Electronics SKU : COM-00529 (and others)
  Keyes Relay: The Keyes 5V relay module is suitable for SCM development, home appliance control. It uses a 5V~12V TIL control signal which can control DC / AC signal.
  TSOP312.., 314..: The TSOP312.., TSOP314.. series are miniaturized receivers for infrared remote control systems. A PIN diode and a preamplifier are assembled on a lead frame, the epoxy package acts as an IR filter. The demodulated output signal can be directly decoded by a microprocessor. The TSOP312.. is compatible with all common IR remote control data formats. The TSOP314.. is optimized to suppress almost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
