# Fritzing sketch Deauther-OLED-RGB_Circuit (saved by Fritzing 0.9.3b)
breadboards: 1

parts:
  U1 = NodeMCU V1.0
  Squix1 = OLED 0.96" 128x64 I2C SSD1306
  S6 = Momentary Switch [package=ksa_sealed_tac_switch]
  S7 = Momentary Switch [package=ksa_sealed_tac_switch]
  S8 = Momentary Switch [package=ksa_sealed_tac_switch]
  LED1 = RGB LED (com. cathode, rgb) [package="5 mm [THT]"]

nets:
  N1: U1.D1, Squix1.SCA
  N2: U1.D2, Squix1.SCL
  N3: U1.D3, S8.1
  N4: U1.D5, S7.1
  N5: U1.D6, LED1.common_cathode
  N6: U1.D7, LED1.green_anode
  N7: U1.D8, LED1.blue_anode
  N8: U1.SD3, S6.4
  N9: Squix1.GND, S6.1, S7.4, S8.4, LED1.red_anode

notes:
  Up
  Select
  Down
  Red
  Blue
  Green

custom parts:
  NodeMCU V1.0: ESP8266 based NodeMCU
