# Fritzing sketch Battery_Doc_Circuit (saved by Fritzing 0.9.3b)
breadboards: 1

parts:
  Part1 = Current Sensor 5A
  U1 = NodeMCU V1.0
  KY-1 = Keyes Relay [package=THT]
  DHT1 = DHT11 Humitidy and Temperature Sensor
  KY-2 = Keyes Relay [package=THT]
  KY-3 = Keyes Relay [package=THT]
  R5 = Resistor [tolerance=±5% resistance=220 package=THT]
  J1 = Piezo Speaker
  o1 = Module display OLED I2C 128x64 SSD1306 [package=THT]
  S1 = Toggle Switch [package=THT]
  ULN2003A1 = ULN2003A [package="DIP (Dual Inline)"]
  JACK1 = 2.1mm Barrel Jack with Terminal Block
  JACK2 = 2.1mm Barrel Jack with Terminal Block
  JACK3 = 2.1mm Barrel Jack with Terminal Block
  R6 = Resistor [tolerance=±5% resistance=220 package=THT]
  R7 = Resistor [tolerance=±5% resistance=220 package=THT]
  R8 = Resistor [tolerance=±5% resistance=220 package=THT]

nets:
  N1: Part1.1, KY-2.C, JACK2.POS, R8.Pin_1
  N2: Part1.2, Part1.OUT, KY-1.NO, KY-3.NO
  VCC: Part1.VCC, U1.3V3, DHT1.VDD, o1.VCC
  GND: Part1.GND, U1.GND, DHT1.GND, R5.Pin_1, J1.pin1, o1.GND, ULN2003A1.GND, JACK1.NEG, JACK2.NEG, JACK3.NEG, R7.Pin_1
  N3: U1.D0, J1.pin2
  N4: U1.D1, o1.SCL
  N5: U1.D2, o1.SDA
  N6: U1.D3, DHT1.DATA
  N7: U1.D5, R6.Pin_0
  N8: U1.D6, ULN2003A1.IN_3, ULN2003A1.IN_4
  N9: U1.D7, ULN2003A1.IN_1
  N10: U1.D8, ULN2003A1.IN_2
  N11: U1.A0, KY-3.C
  N12: KY-1.power, KY-2.power, KY-3.power, S1.L2, ULN2003A1.Common_free_wheeling_diodes
  N13: KY-1.ground, ULN2003A1.OUT_2
  N14: KY-1.C, JACK3.POS
  N15: KY-2.ground, ULN2003A1.OUT_4, ULN2003A1.OUT_3
  N16: KY-2.NO, JACK1.POS, R6.Pin_1
  N17: KY-3.ground, ULN2003A1.OUT_1
  N18: KY-3.NC, R7.Pin_0, R8.Pin_0

notes:
  12V Supply
  To Charger
  To Battery
  To
  Load

custom parts:
  NodeMCU V1.0: ESP8266 based NodeMCU
  Keyes Relay: The Keyes 5V relay module is suitable for SCM development, home appliance control. It uses a 5V~12V TIL control signal which can control DC / AC signal.
  DHT11 Humitidy and Temperature Sensor: DHT11 Humidity and Temperature Sensor
  Module display OLED I2C 128x64 SSD1306: Ecran OLED I2C SSD163 de 128x64 avec connexion I2C
  ULN2003A: The ULN2001A, ULN2002A, ULN2003 and ULN2004A are high voltage, high current darlington arrays each containing seven open collector darlington pairs with common emitters. Each channel rated at 500mA and can withstand peak currents of 600mA. Suppression diodes are included for inductive load driving and the inputs are pinned opposite the outputs to simplify board layout.
